# Fritzing sketch FND_4digit (saved by Fritzing 0.9.3b)
breadboards: 1

parts:
  R1 = Resistor [tolerance=±5% resistance=330 package=THT]
  R2 = Resistor [tolerance=±5% resistance=330 package=THT]
  R3 = Resistor [tolerance=±5% resistance=330 package=THT]
  R4 = Resistor [tolerance=±5% resistance=330 package=THT]
  R5 = Resistor [tolerance=±5% resistance=330 package=THT]
  R6 = Resistor [tolerance=±5% resistance=330 package=THT]
  R7 = Resistor [tolerance=±5% resistance=330 package=THT]
  R8 = Resistor [tolerance=±5% resistance=330 package=THT]
  부품1 = Arduino Uno (Rev3)
  U1 = 7-SEGMENT-4DIGIT [package=7-segment-4digit-5641]

nets:
  N1: R1.Pin_0, R3.Pin_0, R5.Pin_0, R6.Pin_0, R8.Pin_0
  N2: R1.Pin_1, R3.Pin_1, R5.Pin_1, R6.Pin_1, R8.Pin_1
  N3: R2.Pin_0, R4.Pin_0, R7.Pin_0
  N4: R2.Pin_1, R4.Pin_1, R7.Pin_1
  N5: 부품1.D10_PWM/SS, U1.DIG1
  N6: 부품1.D11_PWM/MOSI, U1.DIG2
  N7: 부품1.D12/MISO, U1.DIG3
  N8: 부품1.D13/SCK, U1.DIG4

custom parts:
  7-SEGMENT-4DIGIT: if you need make parts, send me e-mail and write. Price 1 part=0.9 WMZ (http://www.wmtransfer.com/) ~ 0.9 Euro
